// Logisim project pc jmp.circ as structural Verilog: 1 circuit, main circuit main
module main (
);

  wire clock_1_out, clock_2_out, JMP, skok;
  wire [1:0] Dreg, Sreg;
  wire [3:0] Icode;
  wire [7:0] adder_1_out, Adres, multiplexer_1_out, register_1_q;

  Adder adder_1 (.a(register_1_q), .b(8'h1), .out(adder_1_out));  // open: cin, cout
  Decoder #(.select(4)) decoder_1 (
    .out15(JMP), .sel(Icode));  // open: out0, out1, out2, out3, out4, out5, out6, out7, out8, out9, out10, out11, out12, out13, out14, en
  Multiplexer #(.width(8)) multiplexer_1 (
    .in0(adder_1_out), .in1(Adres), .out(multiplexer_1_out), .sel(skok));  // open: en
  Clock clock_1 (.out(clock_1_out));
  Register register_1 (.D(multiplexer_1_out), .Q(register_1_q), .clk(clock_1_out));  // open: en, clr
  buf OR (skok, JMP);  // OR_Gate
  Clock clock_2 (.out(clock_2_out));
  RAM #(.dataWidth(16)) ram_1 (
    .addr(register_1_q), .data({Adres, Icode, Sreg, Dreg}), .clk(clock_2_out));  // open: sel, ld, clr
endmodule
